// Logisim project 4_16_decoder.circ as structural Verilog: 1 circuit, main circuit main
module main (
  input  in_1,
  input  in_2,
  input  in_3,
  input  in_4,
  output out_5,
  output out_6,
  output out_7,
  output out_8,
  output out_9,
  output out_10,
  output out_11,
  output out_12,
  output out_13,
  output out_14,
  output out_15,
  output out_16,
  output out_17,
  output out_18,
  output out_19,
  output out_20
);

  wire and_1_out, and_3_out, and_5_out, and_6_out, and_7_out, and_9_out, and_11_out, and_12_out, not_1_out,
       not_2_out, not_3_out, not_4_out;

  not not_1 (not_1_out, in_1);
  not not_2 (not_2_out, in_2);
  not not_3 (not_3_out, in_3);
  not not_4 (not_4_out, in_4);
  and and_1 (and_1_out, not_1_out, not_2_out);
  and and_2 (and_1_out, not_1_out, not_2_out);
  and and_3 (and_3_out, not_1_out, in_2);
  and and_4 (and_3_out, not_1_out, in_2);
  and and_5 (and_5_out, in_1, not_2_out);
  and and_6 (and_6_out, in_1, in_2);
  and and_7 (and_7_out, not_3_out, not_4_out);
  and and_8 (and_7_out, not_3_out, not_4_out);
  and and_9 (and_9_out, not_3_out, in_4);
  and and_10 (and_9_out, not_3_out, in_4);
  and and_11 (and_11_out, in_3, not_4_out);
  and and_12 (and_12_out, in_3, in_4);
  and and_13 (out_5, and_6_out, and_12_out);
  and and_14 (out_6, and_6_out, and_11_out);
  and and_15 (out_7, and_6_out, and_9_out);
  and and_16 (out_8, and_6_out, and_7_out);
  and and_17 (out_9, and_5_out, and_12_out);
  and and_18 (out_10, and_5_out, and_11_out);
  and and_19 (out_11, and_5_out, and_9_out);
  and and_20 (out_12, and_5_out, and_7_out);
  and and_21 (out_13, and_3_out, and_12_out);
  and and_22 (out_14, and_3_out, and_11_out);
  and and_23 (out_15, and_3_out, and_9_out);
  and and_24 (out_16, and_3_out, and_7_out);
  and and_25 (out_17, and_1_out, and_12_out);
  and and_26 (out_18, and_1_out, and_11_out);
  and and_27 (out_19, and_1_out, and_9_out);
  and and_28 (out_20, and_1_out, and_7_out);
endmodule
