// Logisim project FA.circ as structural Verilog
module fa (
  input  Cin,
  input  ADD_SRC_2,
  input  ADD_SRC_1,
  output S,
  output Cout
);

  wire and_1_out, and_2_out, and_3_out, xor_1_out;

  xor xor_1 (xor_1_out, ADD_SRC_2, ADD_SRC_1);
  and and_1 (and_1_out, Cin, ADD_SRC_2);
  and and_2 (and_2_out, Cin, ADD_SRC_1);
  and and_3 (and_3_out, ADD_SRC_2, ADD_SRC_1);
  xor xor_2 (S, Cin, xor_1_out);
  or or_1 (Cout, and_1_out, and_2_out, and_3_out);
endmodule

module fa_4 (
  input  [3:0] add1,
  input  [3:0] add2,
  output [3:0] sum,
  output carry
);

  wire fa_1_cout, fa_2_cout, fa_3_cout;

  Hex_Digit_Display hex_digit_display_1 (.value(add1));  // open: dp
  Hex_Digit_Display hex_digit_display_2 (.value(add2));  // open: dp
  fa fa_1 (.Cin(1'b0), .ADD_SRC_2(add2[0]), .ADD_SRC_1(add1[0]), .S(sum[0]), .Cout(fa_1_cout));
  Hex_Digit_Display hex_digit_display_3 (.value(sum));  // open: dp
  LED led_1 (.in(carry));
  fa fa_2 (.Cin(fa_1_cout), .ADD_SRC_2(add2[1]), .ADD_SRC_1(add1[1]), .S(sum[1]), .Cout(fa_2_cout));
  fa fa_3 (.Cin(fa_2_cout), .ADD_SRC_2(add2[2]), .ADD_SRC_1(add1[2]), .S(sum[2]), .Cout(fa_3_cout));
  fa fa_4 (.Cin(fa_3_cout), .ADD_SRC_2(add2[3]), .ADD_SRC_1(add1[3]), .S(sum[3]), .Cout(carry));
endmodule
