// Logisim project compare_c.circ as structural Verilog: 4 circuits, main circuit compare
module compare (
);

  wire dipswitch_1_p1, dipswitch_1_p2, dipswitch_1_p3, dipswitch_1_p4, dipswitch_2_p1, dipswitch_2_p2,
       dipswitch_2_p3, dipswitch_2_p4, not_1_out, or_1_out, xor_1_out, xor_2_out, xor_3_out, xor_4_out;

  // DipSwitch #(.number(4)) dipswitch_1: pin names not known; wires that end beside it: dipswitch_1_p1, dipswitch_1_p2, dipswitch_1_p3, dipswitch_1_p4
  // DipSwitch #(.number(4)) dipswitch_2: pin names not known; wires that end beside it: dipswitch_2_p1, dipswitch_2_p2, dipswitch_2_p3, dipswitch_2_p4
  xor xor_1 (xor_1_out, dipswitch_1_p1, dipswitch_2_p1);
  xor xor_2 (xor_2_out, dipswitch_1_p2, dipswitch_2_p2);
  xor xor_3 (xor_3_out, dipswitch_1_p3, dipswitch_2_p3);
  xor xor_4 (xor_4_out, dipswitch_1_p4, dipswitch_2_p4);
  or or_1 (or_1_out, xor_1_out, xor_2_out, xor_3_out, xor_4_out);
  not not_1 (not_1_out, or_1_out);
  LED led_1 (.in(not_1_out));
endmodule

module select_c (
  input  D1,
  input  S,
  input  D0,
  output O
);

  wire and_1_out, and_2_out, not_1_out;

  not not_1 (not_1_out, S);
  and and_1 (and_1_out, D1, S);
  and and_2 (and_2_out, not_1_out, D0);
  or or_1 (O, and_1_out, and_2_out);
endmodule

module select_4to1 (
  input  [1:0] SEL,
  input  [3:0] DIN,
  output out_3
);

  wire select_c_1_o, select_c_2_o;

  select_c select_c_1 (.D1(DIN[3]), .S(SEL[0]), .D0(DIN[2]), .O(select_c_1_o));
  select_c select_c_2 (.D1(DIN[1]), .S(SEL[0]), .D0(DIN[0]), .O(select_c_2_o));
  select_c select_c_3 (.D1(select_c_1_o), .S(SEL[1]), .D0(select_c_2_o), .O(out_3));
endmodule

module select_4to1_3 (
  input  [1:0] in_1,
  input  [3:0] in_2,
  input  [1:0] in_3,
  input  [3:0] in_4,
  input  [1:0] in_5,
  input  [3:0] in_6,
  output out_7,
  output out_8,
  output out_9
);

  select_4to1 select_4to1_1 (.SEL(in_1), .DIN(in_2), .out_3(out_7));
  select_4to1 select_4to1_2 (.SEL(in_3), .DIN(in_4), .out_3(out_8));
  select_4to1 select_4to1_3 (.SEL(in_5), .DIN(in_6), .out_3(out_9));
endmodule
