// Logisim project digit_display.circ as structural Verilog: 1 circuit, main circuit display
module display (
  input  [3:0] in_1
);

  wire and_1_out, and_2_out, and_3_out, and_4_out, and_5_out, and_6_out, and_7_out, and_8_out, not_1_out,
       not_2_out, not_3_out, not_4_out, S_A_out, S_B_out, S_C_out, S_D_out, S_E_out, S_F_out, S_G_out,
       V0_out, V1_out, V2_out, V3_out, V4_out, V5_out, V6_out, V7_out, V8_out, V9_out, VA_out, VB_out,
       VC_out, VD_out, VE_out, VF_out;

  not not_1 (not_1_out, in_1[3]);
  not not_2 (not_2_out, in_1[2]);
  not not_3 (not_3_out, in_1[1]);
  not not_4 (not_4_out, in_1[0]);
  and and_1 (and_1_out, not_1_out, not_2_out);
  and and_2 (and_2_out, not_1_out, in_1[2]);
  and and_3 (and_3_out, in_1[3], not_2_out);
  and and_4 (and_4_out, in_1[3], in_1[2]);
  and and_5 (and_5_out, not_3_out, not_4_out);
  and and_6 (and_6_out, not_3_out, in_1[0]);
  and and_7 (and_7_out, in_1[1], not_4_out);
  and and_8 (and_8_out, in_1[1], in_1[0]);
  and VF (VF_out, and_4_out, and_8_out);
  and VE (VE_out, and_4_out, and_7_out);
  and VD (VD_out, and_4_out, and_6_out);
  and VC (VC_out, and_4_out, and_5_out);
  and VB (VB_out, and_3_out, and_8_out);
  and VA (VA_out, and_3_out, and_7_out);
  and V9 (V9_out, and_3_out, and_6_out);
  and V8 (V8_out, and_3_out, and_5_out);
  and V7 (V7_out, and_2_out, and_8_out);
  and V6 (V6_out, and_2_out, and_7_out);
  and V5 (V5_out, and_2_out, and_6_out);
  and V4 (V4_out, and_2_out, and_5_out);
  and V3 (V3_out, and_1_out, and_8_out);
  and V2 (V2_out, and_1_out, and_7_out);
  and V1 (V1_out, and_1_out, and_6_out);
  and V0 (V0_out, and_1_out, and_5_out);
  or S_G (S_G_out, VB_out, VA_out, V9_out, V8_out, V6_out, V5_out, V4_out, V3_out, V2_out, VE_out, VF_out);
  or S_F (S_F_out, VC_out, VB_out, VA_out, V9_out, V8_out, V6_out, V5_out, V4_out, V1_out, V0_out, VE_out, VF_out);
  or S_E (S_E_out, VF_out, VD_out, VC_out, VB_out, V8_out, VA_out, V6_out, V2_out, V1_out, V0_out, VE_out);
  or S_D (S_D_out, VD_out, VC_out, V9_out, V8_out, V6_out, VB_out, V5_out, V2_out, V3_out, V0_out, VE_out);
  or S_C (S_C_out, VA_out, V9_out, V8_out, V7_out, V6_out, VB_out, V5_out, V4_out, V3_out, V0_out, VD_out);
  or S_B (S_B_out, VA_out, V9_out, V8_out, V7_out, VD_out, V4_out, V3_out, V2_out, V0_out);
  or S_A (S_A_out, VF_out, VE_out, VC_out, V8_out, VA_out, V9_out, V7_out, V6_out, V5_out, V3_out, V2_out, V0_out);
  _7_Segment_Display u_7_segment_display_1 (
    .g(S_G_out), .f(S_F_out), .a(S_A_out), .b(S_B_out), .e(S_E_out), .d(S_D_out), .c(S_C_out));  // open: dp
endmodule
