// Logisim project fa_sign_c.circ as structural Verilog
module fa_sign (
  input  [3:0] SRC2,
  input  [3:0] SRC1,
  output out_3,
  output [3:0] out_4
);

  wire xor_1_out;
  wire [2:0] fa_3_1_sum;

  xor xor_1 (xor_1_out, SRC2[3], SRC1[3]);
  compare1 compare1_1 (.SRC0(SRC1[2]), .SRC1(SRC2[2]));  // open: DOUT
  fa_3 fa_3_1 (.ADD_SRC2(SRC2[2:0]), .ADD_SRC1(SRC1[2:0]), .SUM(fa_3_1_sum), .COUT(out_3));
  select_3bit_1select select_3bit_1select_1 (.S(xor_1_out), .SRC0(fa_3_1_sum), .DOUT(out_4[2:0]));  // open: SRC1

  assign out_4[3] = SRC1[3];
endmodule

module fa_3 (
  input  [2:0] ADD_SRC2,
  input  [2:0] ADD_SRC1,
  output [2:0] SUM,
  output COUT
);

  wire fa_1_cout, fa_2_cout;

  fa fa_1 (.Cin(1'b0), .ADD_SRC_2(ADD_SRC2[0]), .ADD_SRC_1(ADD_SRC1[0]), .S(SUM[0]), .Cout(fa_1_cout));
  fa fa_2 (.Cin(fa_1_cout), .ADD_SRC_2(ADD_SRC2[1]), .ADD_SRC_1(ADD_SRC1[1]), .S(SUM[1]), .Cout(fa_2_cout));
  fa fa_3 (.Cin(fa_2_cout), .ADD_SRC_2(ADD_SRC2[2]), .ADD_SRC_1(ADD_SRC1[2]), .S(SUM[2]), .Cout(COUT));
endmodule

module select_3bit_1select (
  input  [2:0] SRC1,
  input  S,
  input  [2:0] SRC0,
  output [2:0] DOUT
);

  select_c select_c_1 (.D1(SRC1[0]), .S(S), .D0(SRC0[0]), .O(DOUT[0]));
  select_c select_c_2 (.D1(SRC1[1]), .S(S), .D0(SRC0[1]), .O(DOUT[1]));
  select_c select_c_3 (.D1(SRC1[2]), .S(S), .D0(SRC0[2]), .O(DOUT[2]));
endmodule

module compare1 (
  input  SRC0,
  input  SRC1,
  output DOUT
);

  wire xor_1_out;

  xor xor_1 (xor_1_out, SRC0, SRC1);
  not not_1 (DOUT, xor_1_out);
endmodule
