// Logisim project minus_c.circ as structural Verilog: 2 circuits, main circuit minus
module minus (
  input  Bin,
  input  Min,
  input  Sub,
  output Bout,
  output Diff
);

  wire and_1_out, and_2_out, not_1_out, or_1_out, xor_1_out;

  not not_1 (not_1_out, Min);
  or or_1 (or_1_out, Bin, Sub);
  and and_1 (and_1_out, Min, Bin, Sub);
  and and_2 (and_2_out, not_1_out, or_1_out);
  xor xor_1 (xor_1_out, Min, Sub);
  or or_2 (Bout, and_1_out, and_2_out);
  xor xor_2 (Diff, Bin, xor_1_out);
endmodule

module minus_4 (
  input  [3:0] min,
  input  [3:0] sub,
  output bout,
  output [3:0] diff
);

  wire minus_1_bout, minus_2_bout, minus_3_bout;

  Hex_Digit_Display hex_digit_display_1 (.value(min));  // open: dp
  minus minus_1 (.Bin(1'b0), .Min(min[0]), .Sub(sub[0]), .Bout(minus_1_bout), .Diff(diff[0]));
  Hex_Digit_Display hex_digit_display_2 (.value(sub));  // open: dp
  Hex_Digit_Display hex_digit_display_3 (.value(diff));  // open: dp
  minus minus_2 (.Bin(minus_1_bout), .Min(min[1]), .Sub(sub[1]), .Bout(minus_2_bout), .Diff(diff[1]));
  LED led_1 (.in(bout));
  minus minus_3 (.Bin(minus_2_bout), .Min(min[2]), .Sub(sub[2]), .Bout(minus_3_bout), .Diff(diff[2]));
  minus minus_4 (.Bin(minus_3_bout), .Min(min[3]), .Sub(sub[3]), .Bout(bout), .Diff(diff[3]));
endmodule
