// Logisim project or_gate.circ as structural Verilog: 1 circuit, main circuit main
module main (
  input  input0,
  input  input1,
  output out_3
);

  wire and_1_out, and_2_out, not_1_out, not_2_out;

  and and_1 (and_1_out, input0, not_1_out);
  not not_1 (not_1_out, input1);
  not not_2 (not_2_out, input0);
  and and_2 (and_2_out, not_2_out, input1);
  or or_1 (out_3, and_1_out, and_2_out);
endmodule
